// Logisim project 16X1 MUX from 2X1MUX.circ as structural Verilog: 1 circuit, main circuit main
module main (
  input  So,
  input  S1,
  input  S2,
  input  S3,
  input  Io,
  input  I1,
  input  I2,
  input  I3,
  input  I4,
  input  I5,
  input  I6,
  input  I7,
  input  I8,
  input  I9,
  input  I10,
  input  I11,
  input  I12,
  input  I13,
  input  I14,
  input  I15,
  output out_21
);

  wire and_1_out, and_2_out, and_3_out, and_4_out, and_5_out, and_6_out, and_7_out, and_8_out, and_9_out,
       and_10_out, and_11_out, and_12_out, and_13_out, and_14_out, and_15_out, and_16_out, and_17_out,
       and_18_out, and_19_out, and_20_out, and_21_out, and_22_out, and_23_out, and_24_out, and_25_out,
       and_26_out, and_27_out, and_28_out, and_29_out, and_30_out, not_1_out, not_2_out, not_3_out,
       not_4_out, or_1_out, or_2_out, or_3_out, or_4_out, or_5_out, or_6_out, or_7_out, or_8_out, or_9_out,
       or_10_out, or_11_out, or_12_out, or_13_out, or_14_out;

  not not_1 (not_1_out, So);
  and and_1 (and_1_out, Io, not_1_out);
  and and_2 (and_2_out, I1, So);
  and and_3 (and_3_out, I2, not_1_out);
  and and_4 (and_4_out, I3, So);
  and and_5 (and_5_out, I4, not_1_out);
  and and_6 (and_6_out, I5, So);
  and and_7 (and_7_out, I6, not_1_out);
  and and_8 (and_8_out, I7, So);
  and and_9 (and_9_out, I8, not_1_out);
  and and_10 (and_10_out, I9, So);
  and and_11 (and_11_out, I10, not_1_out);
  and and_12 (and_12_out, I11, So);
  and and_13 (and_13_out, I12, not_1_out);
  and and_14 (and_14_out, I13, So);
  and and_15 (and_15_out, I14, not_1_out);
  and and_16 (and_16_out, I15, So);
  or or_1 (or_1_out, and_1_out, and_2_out);
  or or_2 (or_2_out, and_3_out, and_4_out);
  or or_3 (or_3_out, and_5_out, and_6_out);
  or or_4 (or_4_out, and_7_out, and_8_out);
  or or_5 (or_5_out, and_9_out, and_10_out);
  or or_6 (or_6_out, and_11_out, and_12_out);
  or or_7 (or_7_out, and_13_out, and_14_out);
  or or_8 (or_8_out, and_15_out, and_16_out);
  not not_2 (not_2_out, S1);
  and and_17 (and_17_out, or_1_out, not_2_out);
  and and_18 (and_18_out, or_2_out, S1);
  and and_19 (and_19_out, or_3_out, not_2_out);
  or or_9 (or_9_out, and_19_out, and_20_out);
  and and_20 (and_20_out, or_4_out, S1);
  and and_21 (and_21_out, or_5_out, not_2_out);
  or or_10 (or_10_out, and_21_out, and_22_out);
  and and_22 (and_22_out, or_6_out, S1);
  and and_23 (and_23_out, or_7_out, not_2_out);
  or or_11 (or_11_out, and_23_out, and_24_out);
  and and_24 (and_24_out, or_8_out, S1);
  not not_3 (not_3_out, S2);
  or or_12 (or_12_out, and_17_out, and_18_out);
  and and_25 (and_25_out, or_12_out, not_3_out);
  or or_13 (or_13_out, and_25_out, and_26_out);
  and and_26 (and_26_out, or_9_out, S2);
  and and_27 (and_27_out, or_10_out, not_3_out);
  or or_14 (or_14_out, and_27_out, and_28_out);
  and and_28 (and_28_out, or_11_out, S2);
  not not_4 (not_4_out, S3);
  and and_29 (and_29_out, or_13_out, not_4_out);
  and and_30 (and_30_out, or_14_out, S3);
  or or_15 (out_21, and_29_out, and_30_out);
endmodule
