// Logisim project 16X1 MUX.circ as structural Verilog: 1 circuit, main circuit main
module main (
  input  in_1,
  input  in_2,
  input  in_3,
  input  in_4,
  input  in_5,
  input  in_6,
  input  in_7,
  input  in_8,
  input  in_9,
  input  in_10,
  input  in_11,
  input  in_12,
  input  in_13,
  input  S2,
  input  S3,
  input  in_16,
  input  in_17,
  input  in_18,
  input  So,
  input  S1,
  output out_21
);

  wire main_1_o_p, main_2_o_p, main_3_o_p, main_4_o_p;

  _4X1_MUX_main main_1 (.Io(in_1), .I1(in_2), .I2(in_3), .I3(in_4), .S1(So), .So(S1), .o_p(main_1_o_p));
  _4X1_MUX_main main_2 (.Io(in_5), .I1(in_6), .I2(in_7), .I3(in_8), .S1(So), .So(S1), .o_p(main_2_o_p));
  _4X1_MUX_main main_3 (.Io(in_9), .I1(in_10), .I2(in_11), .I3(in_12), .S1(So), .So(S1), .o_p(main_3_o_p));
  _4X1_MUX_main main_4 (.Io(in_13), .I1(in_16), .I2(in_17), .I3(in_18), .S1(So), .So(S1), .o_p(main_4_o_p));
  _4X1_MUX_main main_5 (
    .Io(main_1_o_p), .I1(main_2_o_p), .I2(main_3_o_p), .I3(main_4_o_p), .S1(S2), .So(S3), .o_p(out_21));
endmodule
