// Logisim project 2-bit magnitude comparator.circ as structural Verilog: 1 circuit, main circuit main
module main (
  input  A1,
  input  Ao,
  input  B1,
  input  Bo,
  output A_B,
  output A_B_2,
  output A_B_3
);

  wire and_1_out, and_2_out, and_3_out, and_4_out, and_5_out, and_6_out, not_1_out, not_2_out, not_3_out,
       not_4_out, not_5_out, not_6_out, xor_1_out, xor_2_out;

  not not_1 (not_1_out, A1);
  not not_2 (not_2_out, B1);
  not not_3 (not_3_out, Ao);
  not not_4 (not_4_out, Bo);
  and and_1 (and_1_out, not_1_out, B1);
  and and_2 (and_2_out, not_3_out, B1, Bo);
  and and_3 (and_3_out, not_1_out, not_3_out, Bo);
  xor xor_1 (xor_1_out, Ao, Bo);
  xor xor_2 (xor_2_out, A1, B1);
  and and_4 (and_4_out, A1, not_2_out);
  and and_5 (and_5_out, not_2_out, not_4_out, Ao);
  and and_6 (and_6_out, A1, Ao, not_4_out);
  not not_5 (not_5_out, xor_1_out);
  not not_6 (not_6_out, xor_2_out);
  or or_1 (A_B, and_1_out, and_2_out, and_3_out);
  and and_7 (A_B_2, not_5_out, not_6_out);
  or or_2 (A_B_3, and_4_out, and_5_out, and_6_out);
endmodule
