// Logisim project 2X1 MUX.circ as structural Verilog: 1 circuit, main circuit main
module main (
  input  Io,
  input  I1,
  input  So,
  output out_4
);

  wire and_1_out, and_2_out, not_1_out;

  not not_1 (not_1_out, So);
  and and_1 (and_1_out, not_1_out, Io);
  and and_2 (and_2_out, So, I1);
  or or_1 (out_4, and_1_out, and_2_out);
endmodule
