// Logisim project 4 bit full adder-subtractor.circ as structural Verilog: 1 circuit, main circuit main
module main (
  input  in_1,
  input  Ao,
  input  Bo,
  input  A1,
  input  B1,
  input  A2,
  input  B2,
  input  A3,
  input  B3,
  output So,
  output S1,
  output S2,
  output S3,
  output out_14
);

  wire adder_1_cout, adder_2_cout, adder_3_cout, xor_1_out, xor_2_out, xor_3_out, xor_4_out;

  xor xor_1 (xor_1_out, in_1, Bo);
  xor xor_2 (xor_2_out, in_1, B1);
  xor xor_3 (xor_3_out, in_1, B2);
  xor xor_4 (xor_4_out, in_1, B3);
  Adder #(.width(1)) adder_1 (.a(Ao), .b(xor_1_out), .out(So), .cin(in_1), .cout(adder_1_cout));
  Adder #(.width(1)) adder_2 (.a(A1), .b(xor_2_out), .out(S1), .cin(adder_1_cout), .cout(adder_2_cout));
  Adder #(.width(1)) adder_3 (.a(A2), .b(xor_3_out), .out(S2), .cin(adder_2_cout), .cout(adder_3_cout));
  Adder #(.width(1)) adder_4 (.a(A3), .b(xor_4_out), .out(S3), .cin(adder_3_cout), .cout(out_14));
endmodule
