// Logisim project 4 bit full adder.circ as structural Verilog: 1 circuit, main circuit main
module main (
  input  in_1,
  input  Ao,
  input  Bo,
  input  A1,
  input  B1,
  input  A2,
  input  B2,
  input  A3,
  input  B3,
  output So,
  output S1,
  output S2,
  output S3,
  output out_14
);

  wire adder_1_cout, adder_2_cout, adder_3_cout;

  Adder #(.width(1)) adder_1 (.a(Ao), .b(Bo), .out(So), .cin(in_1), .cout(adder_1_cout));
  Adder #(.width(1)) adder_2 (.a(A1), .b(B1), .out(S1), .cin(adder_1_cout), .cout(adder_2_cout));
  Adder #(.width(1)) adder_3 (.a(A2), .b(B2), .out(S2), .cin(adder_2_cout), .cout(adder_3_cout));
  Adder #(.width(1)) adder_4 (.a(A3), .b(B3), .out(S3), .cin(adder_3_cout), .cout(out_14));
endmodule
