// Logisim project 4-bit computer.circ as structural Verilog: 5 circuits, main circuit main
module main (
);

  wire cpu_1_overflow, undriven, undriven_2;
  wire [3:0] cpu_1_out_0, cpu_1_out_1, cpu_1_out_2, cpu_1_out_3, undriven_3, undriven_4;

  CPU cpu_1 (
    .Set(undriven), .Reset(undriven_2), .Address(undriven_3), .Data(undriven_4), .OUT_0(cpu_1_out_0),
    .OUT_1(cpu_1_out_1), .OUT_2(cpu_1_out_2), .OUT_3(cpu_1_out_3), .Overflow(cpu_1_overflow));  // open: Flag_state
endmodule

module ALU (
  input  [3:0] Data,
  input  Set_A,
  input  Set_B,
  input  Set_O,
  input  Reset,
  input  [3:0] Flags,
  output [3:0] Output,
  output Overflow,
  output Overflow_2,
  output [3:0] Full___overflow,
  output Flag
);

  wire comparator_1_eq, comparator_1_gt, comparator_1_lt, multiplexer_2_out, not_3_out, not_4_out, or_2_out,
       or_3_out;
  wire [3:0] adder_1_out, and_1_out, multiplier_1_out, not_1_out, not_2_out, or_1_out, register_1_q,
       register_2_q, register_3_q, shifter_1_out, shifter_2_out, shifter_3_out, shifter_4_out, xor_1_out;

  Register #(.width(4), .trigger("high")) register_1 (
    .D(Data), .Q(register_1_q), .clk(Set_A), .clr(Reset));  // open: en
  Register #(.width(4), .trigger("high")) register_2 (
    .D(Data), .Q(register_2_q), .clk(Set_B), .clr(Reset));  // open: en
  Register #(.width(4), .trigger("high")) register_3 (
    .D(Data), .Q(register_3_q), .clk(Set_O), .clr(Reset));  // open: en
  assign not_1_out = ~register_1_q;  // NOT_Gate not_1, 4 bits wide
  assign not_2_out = ~register_2_q;  // NOT_Gate not_2, 4 bits wide
  assign or_1_out = register_1_q | register_2_q;  // OR_Gate or_1, 4 bits wide
  assign and_1_out = register_1_q & register_2_q;  // AND_Gate and_1, 4 bits wide
  Pull_Resistor pull_resistor_1 (.node(register_2_q));
  Pull_Resistor pull_resistor_2 (.node(register_1_q));
  Pull_Resistor pull_resistor_3 (.node(Flags));
  assign xor_1_out = register_1_q ^ register_2_q;  // XOR_Gate xor_1, 4 bits wide
  Adder #(.width(4)) adder_1 (.a(register_1_q), .b(register_2_q), .out(adder_1_out), .cout(Overflow));  // open: cin
  Multiplier #(.width(4)) multiplier_1 (
    .a(register_1_q), .b(register_2_q), .out(multiplier_1_out), .cout(Full___overflow));  // open: cin
  Shifter #(.width(4)) shifter_1 (.in(register_1_q), .\dist (register_2_q[1:0]), .out(shifter_1_out));
  Shifter #(.width(4), .shift("lr")) shifter_2 (.in(register_1_q), .\dist (register_2_q[1:0]), .out(shifter_2_out));
  Shifter #(.width(4), .shift("rl")) shifter_3 (.in(register_1_q), .\dist (register_2_q[1:0]), .out(shifter_3_out));
  Shifter #(.width(4), .shift("rr")) shifter_4 (.in(register_1_q), .\dist (register_2_q[1:0]), .out(shifter_4_out));
  Comparator #(.width(4), .mode("unsigned")) comparator_1 (
    .a(register_2_q), .b(register_1_q), .gt(comparator_1_gt), .eq(comparator_1_eq), .lt(comparator_1_lt));
  or or_2 (or_2_out, comparator_1_gt, comparator_1_eq);
  not not_3 (not_3_out, comparator_1_eq);
  or or_3 (or_3_out, comparator_1_eq, comparator_1_lt);
  Multiplexer #(.select(4), .width(4), .enable("false")) multiplexer_1 (
    .in0(register_1_q), .in1(register_2_q), .in2(not_1_out), .in3(not_2_out), .in4(or_1_out),
    .in5(and_1_out), .in6(xor_1_out), .in7(adder_1_out), .in8(multiplier_1_out), .in9(Full___overflow),
    .in10(shifter_1_out), .in11(shifter_2_out), .in12(shifter_3_out), .in13(shifter_4_out), .in14(4'b0000),
    .in15(4'b1111), .out(Output), .sel(register_3_q));
  or or_4 (Overflow_2, Full___overflow[0], Full___overflow[1], Full___overflow[2], Full___overflow[3]);
  Multiplexer #(.select(3), .enable("false")) multiplexer_2 (
    .in0(comparator_1_gt), .in1(comparator_1_eq), .in2(comparator_1_lt), .in3(or_2_out), .in4(or_3_out),
    .in5(not_3_out), .in6(1'b0), .in7(1'b1), .out(multiplexer_2_out), .sel(Flags[2:0]));
  Multiplexer #(.enable("false")) multiplexer_3 (.in0(multiplexer_2_out), .in1(not_4_out), .out(Flag), .sel(Flags[3]));
  not not_4 (not_4_out, multiplexer_2_out);
endmodule

// IU
module Input_unit (
  input  _1,
  input  in_2,
  input  in_3,
  input  _8,
  input  Send,
  input  in_6,
  output [3:0] Data,
  output Send_2,
  output out_9,
  output _1_2,
  output out_11,
  output out_12,
  output _8_2
);

  T_Flip_Flop t_ff_1 (.clk(_1), .T(_1), .Q(_1_2));  // open: Qn, preset, reset, en
  T_Flip_Flop t_ff_2 (.clk(in_2), .T(in_2), .Q(Data[2]));  // open: Qn, preset, reset, en
  T_Flip_Flop t_ff_3 (.clk(in_3), .T(in_3), .Q(Data[1]));  // open: Qn, preset, reset, en
  T_Flip_Flop t_ff_4 (.clk(_8), .T(_8), .Q(_8_2));  // open: Qn, preset, reset, en

  assign {Data[3], Data[0]} = {_1_2, _8_2};
  assign out_9 = in_6;
  assign out_11 = Data[2];
  assign out_12 = Data[1];
  assign Send_2 = Send;
endmodule

module Sub_CPU (
  input  [3:0] Bus_in,
  input  Set_ALU_A,
  input  Set_ALU_B,
  input  Set_ALU_OPC,
  input  Set_flag,
  input  Set_cache,
  input  Set_cache_addr,
  input  Reset,
  input  Set_bus_to_ALU,
  input  Set_bus_to_cache,
  input  Overflow_out,
  output [3:0] Bus_out,
  output Flag,
  output Overflow
);

  wire alu_1_overflow, alu_1_overflow_2, not_1_out, or_2_out;
  wire [3:0] alu_1_full___overflow, alu_1_output, multiplexer_1_out, multiplexer_2_out, multiplexer_3_out,
       ram_1_data, register_1_q, register_2_q;

  Register #(.width(4)) register_1 (.D(Bus_in), .en(1'b1), .Q(register_1_q), .clk(Set_flag), .clr(Reset));
  or or_1 (Overflow, alu_1_overflow, alu_1_overflow_2);
  ALU alu_1 (
    .Data(Bus_in), .Set_A(Set_ALU_A), .Set_B(Set_ALU_B), .Set_O(Set_ALU_OPC), .Reset(Reset),
    .Flags(register_1_q), .Output(alu_1_output), .Overflow(alu_1_overflow), .Overflow_2(alu_1_overflow_2),
    .Full___overflow(alu_1_full___overflow), .Flag(Flag));
  Multiplexer #(.width(4), .enable("false")) multiplexer_1 (
    .in0(alu_1_full___overflow), .in1(4'b0001), .out(multiplexer_1_out), .sel(alu_1_overflow));
  Multiplexer #(.width(4), .enable("false")) multiplexer_2 (
    .in0(alu_1_output), .in1(multiplexer_1_out), .out(multiplexer_2_out), .sel(Overflow_out));
  Register #(.width(4)) register_2 (.D(Bus_in), .en(1'b1), .Q(register_2_q), .clk(Set_cache_addr), .clr(Reset));
  not not_1 (not_1_out, Set_cache);
  Multiplexer #(.width(4), .enable("false")) multiplexer_3 (
    .in0(multiplexer_2_out), .in1(ram_1_data), .out(multiplexer_3_out), .sel(Set_bus_to_cache));
  RAM #(.addrWidth(4), .dataWidth(4), .bus("separate")) ram_1 (
    .addr(register_2_q), .din(Bus_in), .data(ram_1_data), .str(Set_cache), .sel(1'b1), .clk(Set_cache),
    .ld(not_1_out), .clr(Reset));
  or or_2 (or_2_out, Set_bus_to_ALU, Set_bus_to_cache, Overflow_out);
  Register #(.width(4), .trigger("high")) register_3 (
    .D(multiplexer_3_out), .en(1'b1), .Q(Bus_out), .clk(or_2_out), .clr(Reset));
endmodule

module CPU (
  input  Set,
  input  Reset,
  input  [3:0] Address,
  input  [3:0] Data,
  output [3:0] OUT_0,
  output [3:0] OUT_1,
  output [3:0] OUT_2,
  output [3:0] OUT_3,
  output Overflow,
  output Flag_state
);

  wire comparator_1_eq, comparator_2_eq, comparator_3_eq, demultiplexer_1_out1, demultiplexer_1_out2,
       demultiplexer_1_out3, demultiplexer_1_out4, demultiplexer_1_out5, demultiplexer_1_out6,
       demultiplexer_1_out11, demultiplexer_1_out12, demultiplexer_1_out13, demultiplexer_1_out14,
       demultiplexer_1_out15;
  wire [3:0] MOVR_q, multiplexer_1_out, register_1_q, register_2_q, sub_cpu_1_bus_out;

  Demultiplexer #(.select(4), .enable("false")) demultiplexer_1 (
    .out1(demultiplexer_1_out1), .out2(demultiplexer_1_out2), .out3(demultiplexer_1_out3),
    .out4(demultiplexer_1_out4), .out5(demultiplexer_1_out5), .out6(demultiplexer_1_out6),
    .out11(demultiplexer_1_out11), .out12(demultiplexer_1_out12), .out13(demultiplexer_1_out13),
    .out14(demultiplexer_1_out14), .out15(demultiplexer_1_out15), .in(Set), .sel(Address));  // open: out0, out7, out8, out9, out10
  Comparator #(.width(4), .mode("unsigned")) comparator_1 (
    .a(register_1_q), .b(4'b0001), .eq(comparator_1_eq));  // open: gt, lt
  Comparator #(.width(4), .mode("unsigned")) comparator_2 (
    .a(register_1_q), .b(4'b0010), .eq(comparator_2_eq));  // open: gt, lt
  Comparator #(.width(4), .mode("unsigned")) comparator_3 (
    .a(register_1_q), .b(4'b0011), .eq(comparator_3_eq));  // open: gt, lt
  Register #(.width(4)) register_1 (.D(Data), .Q(register_1_q), .clk(demultiplexer_1_out15), .clr(Reset));  // open: en
  Register #(.width(4)) register_2 (.D(Data), .Q(register_2_q), .clk(demultiplexer_1_out6), .clr(Reset));  // open: en
  Sub_CPU sub_cpu_1 (
    .Bus_in(Data), .Set_ALU_A(demultiplexer_1_out1), .Set_ALU_B(demultiplexer_1_out2),
    .Set_ALU_OPC(demultiplexer_1_out3), .Set_flag(demultiplexer_1_out4), .Set_cache(demultiplexer_1_out5),
    .Set_cache_addr(demultiplexer_1_out6), .Reset(Reset), .Set_bus_to_ALU(comparator_1_eq),
    .Set_bus_to_cache(comparator_2_eq), .Overflow_out(comparator_3_eq), .Bus_out(sub_cpu_1_bus_out),
    .Flag(Flag_state), .Overflow(Overflow));
  Multiplexer #(.select(4), .width(4), .enable("false")) multiplexer_1 (
    .in0(4'b0000), .in1(sub_cpu_1_bus_out), .in2(sub_cpu_1_bus_out), .in3(sub_cpu_1_bus_out),
    .in4(register_2_q), .out(multiplexer_1_out), .sel(register_1_q));  // open: in5, in6, in7, in8, in9, in10, in11, in12, in13, in14, in15
  Register #(.width(4)) MOVR (.D(multiplexer_1_out), .Q(MOVR_q), .clk(Reset), .clr(Overflow));  // open: en
  Register #(.width(4)) register_3 (.D(MOVR_q), .Q(OUT_0), .clk(demultiplexer_1_out11), .clr(Reset));  // open: en
  Register #(.width(4)) register_4 (.D(MOVR_q), .Q(OUT_1), .clk(demultiplexer_1_out12), .clr(Reset));  // open: en
  Register #(.width(4)) register_5 (.D(MOVR_q), .Q(OUT_2), .clk(demultiplexer_1_out13), .clr(Reset));  // open: en
  Register #(.width(4)) register_6 (.D(MOVR_q), .Q(OUT_3), .clk(demultiplexer_1_out14), .clr(Reset));  // open: en

  // Notes on the sheet:
  //   ALU OUTPUT
  //   CACHE DATA
  //   ALU OVERFLOW
endmodule
