// Logisim project 4X1 MUX.circ as structural Verilog: 1 circuit, main circuit main
module main (
  input  Io,
  input  I1,
  input  I2,
  input  I3,
  input  S1,
  input  So,
  output o_p
);

  wire main_1_out_4, main_2_out_4;

  _2X1_MUX_main main_1 (.Io(Io), .I1(I1), .So(S1), .out_4(main_1_out_4));
  _2X1_MUX_main main_2 (.Io(I2), .I1(I3), .So(S1), .out_4(main_2_out_4));
  _2X1_MUX_main main_3 (.Io(main_1_out_4), .I1(main_2_out_4), .So(So), .out_4(o_p));
endmodule
