// Logisim project 4bit full subtractor.circ as structural Verilog: 1 circuit, main circuit main
module main (
  input  in_1,
  input  Ao,
  input  Bo,
  input  A1,
  input  B1,
  input  A2,
  input  B2,
  input  A3,
  input  B3,
  output Do,
  output D1,
  output D2,
  output D3,
  output C
);

  wire subtractor_1_bout, subtractor_2_bout, subtractor_3_bout;

  Subtractor #(.width(1)) subtractor_1 (.a(Ao), .b(Bo), .out(Do), .bin(in_1), .bout(subtractor_1_bout));
  Subtractor #(.width(1)) subtractor_2 (.a(A1), .b(B1), .out(D1), .bin(subtractor_1_bout), .bout(subtractor_2_bout));
  Subtractor #(.width(1)) subtractor_3 (.a(A2), .b(B2), .out(D2), .bin(subtractor_2_bout), .bout(subtractor_3_bout));
  Subtractor #(.width(1)) subtractor_4 (.a(A3), .b(B3), .out(D3), .bin(subtractor_3_bout), .bout(C));

  // Notes on the sheet:
  //              0110
  //   0100
  //   1010
endmodule
