// Logisim project 7 segment display.circ as structural Verilog: 2 circuits, main circuit main
module main (
  input  [3:0] in_1
);

  wire segment_1_out_5, segment_1_out_6, segment_1_out_7, segment_1_out_8, segment_1_out_9, segment_1_out_10,
       segment_1_out_11;

  segment segment_1 (
    .in_1(in_1[0]), .in_2(in_1[1]), .in_3(in_1[2]), .in_4(in_1[3]), .out_5(segment_1_out_5),
    .out_6(segment_1_out_6), .out_7(segment_1_out_7), .out_8(segment_1_out_8), .out_9(segment_1_out_9),
    .out_10(segment_1_out_10), .out_11(segment_1_out_11));
  _7_Segment_Display u_7_segment_display_1 (
    .g(segment_1_out_11), .f(segment_1_out_10), .a(segment_1_out_5), .b(segment_1_out_6),
    .e(segment_1_out_9), .d(segment_1_out_8), .c(segment_1_out_7));  // open: dp
endmodule

module segment (
  input  in_1,
  input  in_2,
  input  in_3,
  input  in_4,
  output out_5,
  output out_6,
  output out_7,
  output out_8,
  output out_9,
  output out_10,
  output out_11
);

  wire and_1_out, and_2_out, and_3_out, and_4_out, and_5_out, and_6_out, and_7_out, and_8_out, and_9_out,
       and_10_out, and_11_out, and_12_out, not_1_out, not_2_out, not_3_out, not_4_out, not_5_out, not_6_out,
       not_7_out, not_8_out, not_9_out, not_10_out, or_1_out, xnor_1_out;

  not not_1 (not_1_out, in_2);
  or or_1 (or_1_out, in_4, in_2);
  xnor xnor_1 (xnor_1_out, in_1, in_3);
  and and_1 (and_1_out, in_1, in_2);
  not not_2 (not_2_out, in_1);
  not not_3 (not_3_out, in_2);
  not not_4 (not_4_out, in_3);
  not not_5 (not_5_out, in_3);
  and and_2 (and_2_out, not_2_out, in_2);
  and and_3 (and_3_out, not_2_out, not_4_out);
  not not_6 (not_6_out, in_2);
  not not_7 (not_7_out, in_2);
  not not_8 (not_8_out, in_1);
  and and_4 (and_4_out, not_1_out, in_3);
  and and_5 (and_5_out, not_2_out, not_3_out);
  and and_6 (and_6_out, not_4_out, in_2);
  and and_7 (and_7_out, in_3, in_1, not_6_out);
  and and_8 (and_8_out, not_2_out, not_4_out);
  and and_9 (and_9_out, not_7_out, in_3);
  and and_10 (and_10_out, in_3, not_8_out);
  not not_9 (not_9_out, in_4);
  not not_10 (not_10_out, in_3);
  or or_2 (out_5, or_1_out, xnor_1_out);
  or or_3 (out_6, and_1_out, not_5_out, and_5_out);
  or or_4 (out_8, and_2_out, and_3_out, and_6_out, and_7_out);
  or or_5 (out_9, and_2_out, and_8_out);
  or or_6 (out_10, and_5_out, in_4, and_9_out, and_10_out);
  and and_11 (and_11_out, not_8_out, in_2);
  and and_12 (and_12_out, not_9_out, not_10_out, in_2);
  or or_7 (out_7, in_1, not_3_out, in_3, in_4);
  or or_8 (out_11, in_4, and_11_out, and_4_out, and_12_out);
endmodule
