// Logisim project 7SegDisplay.circ as structural Verilog: 1 circuit, main circuit main
module main (
  input  a3,
  input  a2,
  input  a1,
  input  a0,
  output out_5,
  output out_6,
  output out_7,
  output out_8,
  output out_9,
  output out_10,
  output out_11
);

  _7_segment_display_driver u_7_segment_display_driver_1 (
    .D(a3), .C(a2), .B(a1), .A(a0), .a_2(out_7), .b_2(out_6), .c_2(out_10), .d_2(out_11), .e(out_9),
    .f(out_8), .g(out_5));
endmodule
