// Logisim project ALU.circ as structural Verilog: 1 circuit, main circuit main
module main (
  input  [3:0] A,
  input  [3:0] B,
  input  [3:0] in_3,
  output [3:0] out_4,
  output [2:0] plus_ve_zero__ve
);

  wire [3:0] adder_1_out, adder_2_out, and_1_out, divider_1_out, multiplier_1_out, negator_1_out, not_1_out,
       not_2_out, or_1_out, shifter_1_out, shifter_2_out, shifter_3_out, subtractor_1_out, xor_1_out;

  Adder #(.width(4)) adder_1 (.a(A), .b(B), .out(adder_1_out));  // open: cin, cout
  Subtractor #(.width(4)) subtractor_1 (.a(A), .b(B), .out(subtractor_1_out));  // open: bin, bout
  Multiplier #(.width(4)) multiplier_1 (.a(A), .b(B), .out(multiplier_1_out));  // open: cin, cout
  Divider #(.width(4)) divider_1 (.a(A), .b(B), .out(divider_1_out));  // open: upper, rem
  Negator #(.width(4)) negator_1 (.in(A), .out(negator_1_out));
  assign not_1_out = ~A;  // NOT_Gate not_1, 4 bits wide
  Shifter #(.width(4)) shifter_1 (.in(A), .\dist (2'b10), .out(shifter_1_out));
  Shifter #(.width(4), .shift("lr")) shifter_2 (.in(A), .\dist (2'b10), .out(shifter_2_out));
  Shifter #(.width(4), .shift("ar")) shifter_3 (.in(A), .\dist (2'b10), .out(shifter_3_out));
  assign and_1_out = A & B;  // AND_Gate and_1, 4 bits wide
  assign or_1_out = A | B;  // OR_Gate or_1, 4 bits wide
  Adder #(.width(4)) adder_2 (.a(not_1_out), .b(4'b0001), .out(adder_2_out));  // open: cin, cout
  assign xor_1_out = A ^ B;  // XOR_Gate xor_1, 4 bits wide
  assign not_2_out = ~4'b1111;  // NOT_Gate not_2, 4 bits wide
  Multiplexer #(.select(4), .width(4)) multiplexer_1 (
    .in0(not_2_out), .in1(4'b1111), .in2(A), .in3(B), .in4(adder_1_out), .in5(subtractor_1_out),
    .in6(multiplier_1_out), .in7(divider_1_out), .in8(negator_1_out), .in9(and_1_out), .in10(or_1_out),
    .in11(adder_2_out), .in12(shifter_1_out), .in13(shifter_2_out), .in14(shifter_3_out), .in15(xor_1_out),
    .out(out_4), .sel(in_3));  // open: en
  and and_2 (plus_ve_zero__ve[1], ~out_4[0], ~out_4[1], ~out_4[2], ~out_4[3]);  // AND_Gate
  and and_3 (plus_ve_zero__ve[2], ~plus_ve_zero__ve[1], ~out_4[3]);  // AND_Gate

  assign plus_ve_zero__ve[0] = out_4[3];

  // Notes on the sheet:
  //   0100
  //   0101
  //   0110
  //   0111
  //   1000
  //   1001
  //   1010
  //   1011
  //   1100
  //   1101
  //   1110
  //   1111
endmodule
