// Logisim project D ff using SR ff.circ as structural Verilog: 1 circuit, main circuit main
module main (
  input  in_1,
  output out_2,
  output out_3
);

  wire clock_1_out, not_1_out;

  Clock clock_1 (.out(clock_1_out));
  clocked_SR_ff_main main_1 (.S(in_1), .R(not_1_out), .Q(out_2), .nQ(out_3));
  not not_1 (not_1_out, in_1);
endmodule
