// Logisim project RAM.circ as structural Verilog: 1 circuit, main circuit main
module main (
  input  in_1,
  input  in_2
);

  wire button_1_out, button_2_out, clock_1_out, controlled_buffer_1_out, controlled_buffer_2_out;
  wire [6:0] bitselector_1_out;
  wire [15:0] counter_1_q;
  wire [31:0] ram_1_data, random_1_out;

  assign controlled_buffer_1_out = in_2 ? clock_1_out : 1'bz;  // Controlled_Buffer controlled_buffer_1
  Clock clock_1 (.out(clock_1_out));
  Button button_1 (.out(button_1_out));
  Counter #(.width(16), .max('hffff), .ongoal("stay")) counter_1 (
    .Q(counter_1_q), .clk(controlled_buffer_2_out), .clr(button_1_out));  // open: load, D, count, carry
  Random #(.width(32)) random_1 (.clk(clock_1_out), .out(random_1_out));  // open: next, clr
  RAM #(.addrWidth(16), .dataWidth(32), .bus("separate")) ram_1 (
    .addr(counter_1_q), .din(random_1_out), .data(ram_1_data), .clk(controlled_buffer_1_out));  // open: str, sel, ld, clr
  assign controlled_buffer_2_out = in_1 ? clock_1_out : 1'bz;  // Controlled_Buffer controlled_buffer_2
  BitSelector #(.width(32), .group(7)) bitselector_1 (.in(ram_1_data), .out(bitselector_1_out));  // open: sel
  Button button_2 (.out(button_2_out));
  TTY #(.rows(40), .cols(64)) tty_1 (
    .data(bitselector_1_out), .clk(controlled_buffer_2_out), .clr(button_2_out));  // open: we
endmodule
