// Logisim project RAM8X7.circ as structural Verilog: 1 circuit, main circuit main
module main (
  input  in_1,
  input  in_2
);

  wire button_1_out, clock_1_out, controlled_buffer_1_out, controlled_buffer_2_out;
  wire [6:0] ram_1_data, random_1_out;
  wire [7:0] counter_1_q;

  assign controlled_buffer_1_out = in_1 ? clock_1_out : 1'bz;  // Controlled_Buffer controlled_buffer_1
  Clock clock_1 (.out(clock_1_out));
  Button button_1 (.out(button_1_out));
  Counter #(.ongoal("stay")) counter_1 (
    .Q(counter_1_q), .clk(controlled_buffer_2_out), .clr(button_1_out));  // open: load, D, count, carry
  Random #(.width(7)) random_1 (.clk(clock_1_out), .out(random_1_out));  // open: next, clr
  RAM #(.dataWidth(7), .bus("separate")) ram_1 (
    .addr(counter_1_q), .din(random_1_out), .data(ram_1_data), .clk(controlled_buffer_1_out));  // open: str, sel, ld, clr
  assign controlled_buffer_2_out = in_2 ? clock_1_out : 1'bz;  // Controlled_Buffer controlled_buffer_2
  TTY #(.rows(40)) tty_1 (.data(ram_1_data), .clk(controlled_buffer_2_out));  // open: we, clr
endmodule
