// Logisim project ROM.circ as structural Verilog: 1 circuit, main circuit main
module main (
  input  in_1
);

  wire button_1_out, clock_1_out;
  wire [6:0] bitselector_1_out;
  wire [15:0] counter_1_q;
  wire [31:0] rom_1_data;

  Counter #(.width(16), .max('hffff), .ongoal("stay")) counter_1 (
    .load(in_1), .Q(counter_1_q), .clk(clock_1_out), .clr(button_1_out));  // open: D, count, carry
  Button button_1 (.out(button_1_out));
  Clock clock_1 (.out(clock_1_out));
  ROM #(.addrWidth(16), .dataWidth(32)) rom_1 (.addr(counter_1_q), .data(rom_1_data));  // open: sel
  BitSelector #(.width(32), .group(7)) bitselector_1 (.in(rom_1_data), .out(bitselector_1_out));  // open: sel
  TTY #(.rows(40), .cols(57)) tty_1 (.data(bitselector_1_out), .clk(clock_1_out), .clr(button_1_out));  // open: we

  // Notes on the sheet:
  //   contents of rom_1 (hex, n*v repeats v):
  //   65326532 11111111 67897465 dfcbdfcb 527 0 8741 0 0 5423 0 dfcb 5*0 f7845 0 0 54 33*0 521 66*0 32
  //   43*0 211 13*0 45 0 0 0 452 0 0 0 520 74*0 78 6*0 5421 553*0 5421 141*0 4 15*0 120 0 5421 433*0 b78
  //   113*0 6f
endmodule
