// Logisim project ROM4bit.circ as structural Verilog: 1 circuit, main circuit main
module main (
);

  wire clock_1_out;
  wire [3:0] random_1_out, rom_1_data;
  wire [6:0] bit_extender_1_out;

  Random #(.width(4)) random_1 (.clk(clock_1_out), .out(random_1_out));  // open: next, clr
  ROM #(.addrWidth(4), .dataWidth(4)) rom_1 (.addr(random_1_out), .data(rom_1_data));  // open: sel
  Clock clock_1 (.out(clock_1_out));
  assign bit_extender_1_out = {{3{1'b1}}, rom_1_data};  // Bit_Extender bit_extender_1
  TTY tty_1 (.data(bit_extender_1_out), .clk(clock_1_out));  // open: we, clr

  // Notes on the sheet:
  //   contents of rom_1 (hex, n*v repeats v):
  //   4 0 5 1 3 3 2 0 4 6 3 9
endmodule
