// Logisim project [Digital Circuit] Simple Calculator Display - 12 digit display with buttons 0-9, backspace and clear.circ as structural Verilog: 3 circuits, main circuit left-right shift register is falling edge triggered! (24/12/2011 6:46PM A'bad)
module left_right_shift_register_is_falling_edge_triggered___24_12_2011_6_46PM_A_bad (
);

  wire _0_2_out, _0_3_out, _0_4_out, _0_5_out, _1_2_out, _1_3_out, _1_4_out, _1_5_out, and_1_out, Backspace,
       Clear_All, CLOCK, n0, n1, n2, n3, n4, n5, n6, n7, n8, n9, or_1_out, or_2_out, or_3_out, or_4_out,
       or_5_out, or_6_out, or_7_out, or_8_out, or_9_out, or_10_out, or_11_out, or_12_out, or_13_out,
       or_14_out, t_ff_1_q, t_ff_1_qn, t_ff_2_q, t_ff_2_qn, t_ff_3_q, t_ff_3_qn, t_ff_4_q, t_ff_4_qn;
  wire [3:0] _0, _1, _2, _3, _4, _5, _6, _7, _8, _9, _10, _11;

  Hex_Digit_Display hex_digit_display_1 (.value(_11));  // open: dp
  Hex_Digit_Display hex_digit_display_2 (.value(_10));  // open: dp
  Hex_Digit_Display hex_digit_display_3 (.value(_9));  // open: dp
  Hex_Digit_Display hex_digit_display_4 (.value(_8));  // open: dp
  or or_1 (or_1_out, n8, n6, n4, n2, n0);
  or or_2 (or_2_out, n9, n7, n5, n3, n1);
  or or_3 (or_3_out, n9, n8, n5, n4, n1, n0);
  or or_4 (or_4_out, n7, n6, n3, n2);
  or or_5 (or_5_out, n9, n8, n3, n2, n1, n0);
  or or_6 (or_6_out, n7, n6, n5, n4);
  or or_7 (or_7_out, n7, n6, n5, n4, n3, n2, n1, n0);
  or or_8 (or_8_out, n9, n8);
  Hex_Digit_Display hex_digit_display_5 (.value(_7));  // open: dp
  Hex_Digit_Display hex_digit_display_6 (.value(_6));  // open: dp
  Button u__8 (.out(n8));
  Button u__7 (.out(n7));
  Button u__4 (.out(n4));
  Button u__5 (.out(n5));
  Button u__1 (.out(n1));
  Button u__2 (.out(n2));
  Button u__0 (.out(n0));
  or or_9 (or_9_out, _11[0], _11[1], _11[2], _11[3]);
  and _0_2 (_0_2_out, or_1_out, t_ff_1_q);
  and _1_2 (_1_2_out, t_ff_1_qn, or_2_out);
  and _0_3 (_0_3_out, or_3_out, t_ff_2_q);
  and _1_3 (_1_3_out, t_ff_2_qn, or_4_out);
  and _0_4 (_0_4_out, or_5_out, t_ff_3_q);
  and _1_4 (_1_4_out, t_ff_3_qn, or_6_out);
  and _0_5 (_0_5_out, or_7_out, t_ff_4_q);
  and _1_5 (_1_5_out, t_ff_4_qn, or_8_out);
  Hex_Digit_Display hex_digit_display_7 (.value(_5));  // open: dp
  Hex_Digit_Display hex_digit_display_8 (.value(_4));  // open: dp
  Button u__9 (.out(n9));
  Button u__6 (.out(n6));
  Button u__3 (.out(n3));
  Button CE (.out(Clear_All));
  Button button (.out(Backspace));
  or or_10 (or_10_out, n0, n1, n2, n3, n4, n5, n6, n7, n8, n9);
  T_Flip_Flop t_ff_1 (.clk(or_11_out), .T(1'b1), .Q(t_ff_1_q), .Qn(t_ff_1_qn));  // open: preset, reset, en
  or or_11 (or_11_out, _0_2_out, _1_2_out);
  or or_12 (or_12_out, _0_3_out, _1_3_out);
  T_Flip_Flop t_ff_2 (.clk(or_12_out), .T(1'b1), .Q(t_ff_2_q), .Qn(t_ff_2_qn));  // open: preset, reset, en
  T_Flip_Flop t_ff_3 (.clk(or_13_out), .T(1'b1), .Q(t_ff_3_q), .Qn(t_ff_3_qn));  // open: preset, reset, en
  or or_13 (or_13_out, _0_4_out, _1_4_out);
  or or_14 (or_14_out, _0_5_out, _1_5_out);
  T_Flip_Flop t_ff_4 (.clk(or_14_out), .T(1'b1), .Q(t_ff_4_q), .Qn(t_ff_4_qn));  // open: preset, reset, en
  Hex_Digit_Display hex_digit_display_9 (.value(_2));  // open: dp
  Hex_Digit_Display hex_digit_display_10 (.value(_3));  // open: dp
  and and_1 (and_1_out, or_10_out, ~or_9_out);  // AND_Gate
  _12_bit_left_right_shift_register LSB (
    .Data_in_right_shift(t_ff_1_q), .right_left_shift(Backspace), .CLK(CLOCK),
    .Current_State__12_bits({_11[0], _10[0], _9[0], _8[0], _7[0], _6[0], _5[0], _4[0], _3[0], _2[0], _1[0], _0[0]}),
    .RESET(Clear_All));
  _12_bit_left_right_shift_register u_12_bit_left_right_shift_register_1 (
    .Data_in_right_shift(t_ff_2_q), .right_left_shift(Backspace), .CLK(CLOCK),
    .Current_State__12_bits({_11[1], _10[1], _9[1], _8[1], _7[1], _6[1], _5[1], _4[1], _3[1], _2[1], _1[1], _0[1]}),
    .RESET(Clear_All));
  _12_bit_left_right_shift_register u_12_bit_left_right_shift_register_2 (
    .Data_in_right_shift(t_ff_3_q), .right_left_shift(Backspace), .CLK(CLOCK),
    .Current_State__12_bits({_11[2], _10[2], _9[2], _8[2], _7[2], _6[2], _5[2], _4[2], _3[2], _2[2], _1[2], _0[2]}),
    .RESET(Clear_All));
  _12_bit_left_right_shift_register MSB (
    .Data_in_right_shift(t_ff_4_q), .right_left_shift(Backspace), .CLK(CLOCK),
    .Current_State__12_bits({_11[3], _10[3], _9[3], _8[3], _7[3], _6[3], _5[3], _4[3], _3[3], _2[3], _1[3], _0[3]}),
    .RESET(Clear_All));
  Hex_Digit_Display hex_digit_display_11 (.value(_0));  // open: dp
  Hex_Digit_Display hex_digit_display_12 (.value(_1));  // open: dp
  or or_15 (CLOCK, and_1_out, Backspace);

  // Other names for the same wires on the sheet: bit0[11:0] = {_11[0], _10[0], _9[0], _8[0], _7[0], _6[0], _5[0], _4[0], _3[0], _2[0], _1[0], _0[0]};
  //   bit1[11:0] = {_11[1], _10[1], _9[1], _8[1], _7[1], _6[1], _5[1], _4[1], _3[1], _2[1], _1[1], _0[1]};
  //   bit2[11:0] = {_11[2], _10[2], _9[2], _8[2], _7[2], _6[2], _5[2], _4[2], _3[2], _2[2], _1[2], _0[2]};
  //   bit3[11:0] = {_11[3], _10[3], _9[3], _8[3], _7[3], _6[3], _5[3], _4[3], _3[3], _2[3], _1[3], _0[3]};
  //   LEFT_RIGHT = Backspace

  // Notes on the sheet:
  //   TAKING INPUTS -
  //   Press Buttons and see the BCD display
  //   The Backspace button also works!
  //   BCD Representation -
  //   Making the 12 Digit Display -
  //   For BCD representation, we need 4 bits (to uniquely represent every number from 0 through 9)
  //   The trick was to make the T flip flop rising edge triggered while the
  //   left right shift register is falling edge triggered! (24/12/2011 6:46PM A'bad)
  //   This small OR gate prevents adding
  //   more digits when the 12th bit is non zero
  //    (12 bits - 0 through 11)
endmodule

module l_r_shift (
  input  right_left_shift,
  input  Data_In_Right_Shift,
  input  Data_In_Left_Shift,
  input  CLK,
  input  RESET,
  output [3:0] Current_State_of_Registers,
  output Data_out_Right_Shift,
  output Data_Out_Left_Shift
);

  wire and_1_out, and_2_out, and_3_out, and_4_out, and_5_out, and_6_out, and_7_out, and_8_out, not_1_out,
       or_1_out, or_2_out, or_3_out, or_4_out;

  not not_1 (not_1_out, right_left_shift);
  and and_1 (and_1_out, Current_State_of_Registers[1], right_left_shift);
  or or_1 (or_1_out, and_1_out, and_2_out);
  and and_2 (and_2_out, Data_In_Right_Shift, not_1_out);
  D_Flip_Flop #(.trigger("falling")) LSB (
    .clk(CLK), .D(or_1_out), .Q(Current_State_of_Registers[0]), .reset(RESET));  // open: Qn, preset, en
  and and_3 (and_3_out, Current_State_of_Registers[2], right_left_shift);
  and and_4 (and_4_out, Current_State_of_Registers[0], not_1_out);
  D_Flip_Flop #(.trigger("falling")) d_ff_1 (
    .clk(CLK), .D(or_2_out), .Q(Current_State_of_Registers[1]), .reset(RESET));  // open: Qn, preset, en
  or or_2 (or_2_out, and_3_out, and_4_out);
  and and_5 (and_5_out, Current_State_of_Registers[3], right_left_shift);
  and and_6 (and_6_out, Current_State_of_Registers[1], not_1_out);
  or or_3 (or_3_out, and_5_out, and_6_out);
  D_Flip_Flop #(.trigger("falling")) d_ff_2 (
    .clk(CLK), .D(or_3_out), .Q(Current_State_of_Registers[2]), .reset(RESET));  // open: Qn, preset, en
  and and_7 (and_7_out, Data_In_Left_Shift, right_left_shift);
  or or_4 (or_4_out, and_7_out, and_8_out);
  and and_8 (and_8_out, Current_State_of_Registers[2], not_1_out);
  D_Flip_Flop #(.trigger("falling")) MSB (
    .clk(CLK), .D(or_4_out), .Q(Current_State_of_Registers[3]), .reset(RESET));  // open: Qn, preset, en

  assign Data_Out_Left_Shift = Current_State_of_Registers[0];
  assign Data_out_Right_Shift = Current_State_of_Registers[3];

  // Notes on the sheet:
  //   4 bit left right shift register
endmodule

// Shift
module _12_bit_left_right_shift_register (
  input  Data_in_right_shift,
  input  right_left_shift,
  input  CLK,
  input  RESET,
  output [11:0] Current_State__12_bits
);

  wire l_r_shift_1_data_out_left_shift, l_r_shift_1_data_out_right_shift, LSB_data_out_right_shift,
       MSB_data_out_left_shift;

  l_r_shift LSB (
    .Current_State_of_Registers(Current_State__12_bits[3:0]), .right_left_shift(right_left_shift),
    .Data_In_Right_Shift(Data_in_right_shift), .CLK(CLK),
    .Data_In_Left_Shift(l_r_shift_1_data_out_left_shift), .Data_out_Right_Shift(LSB_data_out_right_shift),
    .RESET(RESET));  // open: Data_Out_Left_Shift
  l_r_shift l_r_shift_1 (
    .Current_State_of_Registers(Current_State__12_bits[7:4]), .right_left_shift(right_left_shift),
    .Data_In_Right_Shift(LSB_data_out_right_shift), .CLK(CLK), .Data_In_Left_Shift(MSB_data_out_left_shift),
    .Data_out_Right_Shift(l_r_shift_1_data_out_right_shift),
    .Data_Out_Left_Shift(l_r_shift_1_data_out_left_shift), .RESET(RESET));
  l_r_shift MSB (
    .Current_State_of_Registers(Current_State__12_bits[11:8]), .right_left_shift(right_left_shift),
    .Data_In_Right_Shift(l_r_shift_1_data_out_right_shift), .CLK(CLK), .Data_In_Left_Shift(1'b0),
    .Data_Out_Left_Shift(MSB_data_out_left_shift), .RESET(RESET));  // open: Data_out_Right_Shift

  // Notes on the sheet:
  //   Current_State__12_bits: pull=up
endmodule
