// Logisim project basicROM.circ as structural Verilog: 1 circuit, main circuit main
module main (
  input  [15:0] in_1,
  input  [31:0] store,
  input  in_3,
  input  [15:0] in_4,
  output [31:0] out_5,
  output [31:0] out_6
);

  wire clock_1_out, not_1_out;

  assign out_6 = in_3 ? store : 32'bz;  // Controlled_Buffer controlled_buffer_1
  ROM #(.addrWidth(16), .dataWidth(32)) rom_1 (.addr(in_1), .data(out_5));  // open: sel
  Clock clock_1 (.out(clock_1_out));
  not not_1 (not_1_out, in_3);
  RAM #(.addrWidth(16), .dataWidth(32)) ram_1 (
    .addr(in_4), .data(out_6), .clk(clock_1_out), .ld(not_1_out));  // open: sel, clr

  // Notes on the sheet:
  //   ROM
  //   data input
  //   address
  //   contents of rom_1 (hex, n*v repeats v):
  //   86453 648532 dfb 78645321
  //   RAM
  //   data output
endmodule
