// Logisim project calculator.circ as structural Verilog
module main (
  input  _1_subtract___0_add,
  input  [3:0] in_2,
  input  [3:0] in_3
);

  wire adder_sub_1_out_10, adder_sub_1_out_11, adder_sub_1_out_12, adder_sub_1_out_13, main_1_out_5,
       main_1_out_6, main_1_out_7, main_1_out_8, main_1_out_9, main_1_out_10, main_1_out_11;

  adder_sub adder_sub_1 (
    .in_1(_1_subtract___0_add), .in_2(in_2[0]), .in_3(in_3[0]), .in_4(in_2[1]), .in_5(in_3[1]),
    .in_6(in_2[2]), .in_7(in_3[2]), .in_8(in_2[3]), .in_9(in_3[3]), .out_10(adder_sub_1_out_10),
    .out_11(adder_sub_1_out_11), .out_12(adder_sub_1_out_12), .out_13(adder_sub_1_out_13));  // open: out_14
  _7SegDisplay_main main_1 (
    .a3(adder_sub_1_out_13), .a2(adder_sub_1_out_12), .a1(adder_sub_1_out_11), .a0(adder_sub_1_out_10),
    .out_9(main_1_out_9), .out_11(main_1_out_11), .out_10(main_1_out_10), .out_5(main_1_out_5),
    .out_8(main_1_out_8), .out_7(main_1_out_7), .out_6(main_1_out_6));
  _7_Segment_Display u_7_segment_display_1 (
    .g(main_1_out_5), .f(main_1_out_8), .a(main_1_out_7), .b(main_1_out_6), .e(main_1_out_9),
    .d(main_1_out_11), .c(main_1_out_10));  // open: dp
endmodule

module full_adder (
  input  in_1,
  input  in_2,
  input  in_3,
  output out_4,
  output out_5
);

  wire and_1_out, and_2_out, and_3_out, xor_1_out;

  and and_1 (and_1_out, in_3, in_2);
  and and_2 (and_2_out, in_2, in_1);
  and and_3 (and_3_out, in_3, in_1);
  xor xor_1 (xor_1_out, in_2, in_1);
  or or_1 (out_4, and_1_out, and_2_out, and_3_out);
  xor xor_2 (out_5, xor_1_out, in_3);
endmodule

module adder_sub (
  input  in_1,
  input  in_2,
  input  in_3,
  input  in_4,
  input  in_5,
  input  in_6,
  input  in_7,
  input  in_8,
  input  in_9,
  output out_10,
  output out_11,
  output out_12,
  output out_13,
  output out_14
);

  wire full_adder_1_out_4, full_adder_2_out_4, full_adder_3_out_4, xor_1_out, xor_2_out, xor_3_out, xor_4_out;

  xor xor_1 (xor_1_out, in_3, in_1);
  xor xor_2 (xor_2_out, in_5, in_1);
  xor xor_3 (xor_3_out, in_7, in_1);
  xor xor_4 (xor_4_out, in_9, in_1);
  full_adder full_adder_1 (.in_1(in_1), .in_2(in_2), .in_3(xor_1_out), .out_4(full_adder_1_out_4), .out_5(out_10));
  full_adder full_adder_2 (
    .in_1(full_adder_1_out_4), .in_2(in_4), .in_3(xor_2_out), .out_4(full_adder_2_out_4), .out_5(out_11));
  full_adder full_adder_3 (
    .in_1(full_adder_2_out_4), .in_2(in_6), .in_3(xor_3_out), .out_4(full_adder_3_out_4), .out_5(out_12));
  full_adder full_adder_4 (.in_1(full_adder_3_out_4), .in_2(in_8), .in_3(xor_4_out), .out_4(out_14), .out_5(out_13));
endmodule
