// Logisim project decoder.circ as structural Verilog: 1 circuit, main circuit main
module main (
  input  w,
  input  x,
  input  y,
  input  z,
  output out_5,
  output out_6,
  output out_7,
  output out_8,
  output out_9,
  output out_10,
  output out_11
);

  wire and_1_out, and_2_out, and_3_out, and_4_out, and_5_out, and_6_out, and_7_out, and_8_out, and_9_out,
       and_10_out, and_11_out, and_12_out, and_13_out, and_14_out, and_15_out, and_16_out, and_17_out,
       and_18_out, not_1_out, not_2_out, not_3_out, not_4_out;

  not not_1 (not_1_out, w);
  not not_2 (not_2_out, x);
  not not_3 (not_3_out, y);
  not not_4 (not_4_out, z);
  and and_1 (and_1_out, not_4_out, x);
  and and_2 (and_2_out, not_3_out, x);
  and and_3 (and_3_out, not_3_out, not_4_out);
  and and_4 (and_4_out, not_1_out, x, z);
  and and_5 (and_5_out, w, not_2_out);
  and and_6 (and_6_out, not_2_out, not_4_out);
  and and_7 (and_7_out, y, z);
  and and_8 (and_8_out, not_3_out, not_4_out);
  and and_9 (and_9_out, not_1_out, z);
  and and_10 (and_10_out, not_2_out, y);
  and and_11 (and_11_out, not_2_out, not_4_out);
  and and_12 (and_12_out, y, not_4_out);
  and and_13 (and_13_out, x, not_3_out, z);
  and and_14 (and_14_out, not_2_out, not_4_out);
  and and_15 (and_15_out, y, not_4_out);
  and and_16 (and_16_out, not_2_out, y);
  and and_17 (and_17_out, y, not_4_out);
  and and_18 (and_18_out, x, not_3_out);
  or or_1 (out_5, w, and_1_out, and_2_out, and_3_out);
  or or_2 (out_6, y, and_4_out, and_5_out, and_6_out);
  or or_3 (out_7, not_2_out, and_7_out, and_8_out);
  or or_4 (out_8, not_3_out, and_9_out, x);
  or or_5 (out_9, w, and_10_out, and_11_out, and_12_out, and_13_out);
  or or_6 (out_10, and_14_out, and_15_out);
  or or_7 (out_11, w, and_16_out, and_17_out, and_18_out);
endmodule
