// Logisim project even parity generator & checker.circ as structural Verilog: 1 circuit, main circuit main
module main (
  input  A,
  input  B,
  input  C,
  input  A_2,
  input  B_2,
  input  C_2,
  input  P,
  output P_2,
  output E
);

  wire xor_1_out, xor_2_out, xor_3_out;

  xor xor_1 (xor_1_out, A, B);
  xor xor_2 (xor_2_out, A_2, B_2);
  xor xor_3 (xor_3_out, C_2, P);
  xor xor_4 (P_2, xor_1_out, C);
  xor xor_5 (E, xor_2_out, xor_3_out);

  // Notes on the sheet:
  //   3-bit parity generator
  //   PARITY CHECKER
endmodule
