// Logisim project full subtractor.circ as structural Verilog: 1 circuit, main circuit main
module main (
  input  A,
  input  B,
  input  C,
  output D,
  output Bo
);

  wire and_1_out, and_2_out, and_3_out, not_1_out, xor_1_out;

  not not_1 (not_1_out, A);
  and and_1 (and_1_out, not_1_out, C);
  xor xor_1 (xor_1_out, A, B);
  and and_2 (and_2_out, B, not_1_out);
  and and_3 (and_3_out, B, C);
  xor xor_2 (D, xor_1_out, C);
  or or_1 (Bo, and_2_out, and_3_out, and_1_out);
endmodule
