// Logisim project odd parity generator & checker.circ as structural Verilog: 1 circuit, main circuit main
module main (
  input  A,
  input  B,
  input  C,
  input  in_4,
  input  in_5,
  input  in_6,
  input  in_7,
  output out_8,
  output out_9
);

  wire xor_1_out, xor_2_out, xor_3_out, xor_4_out, xor_5_out;

  xor xor_1 (xor_1_out, B, C);
  xor xor_2 (xor_2_out, in_4, in_5);
  xor xor_3 (xor_3_out, in_6, in_7);
  xor xor_4 (xor_4_out, A, xor_1_out);
  xor xor_5 (xor_5_out, xor_2_out, xor_3_out);
  not not_1 (out_8, xor_4_out);
  not not_2 (out_9, xor_5_out);

  // Notes on the sheet:
  //   ODD PARITY GENERATOR
  //   ODD PARITY CHECKER
endmodule
