// Logisim project seven segment display.circ as structural Verilog: 1 circuit, main circuit main
module main (
  input  in_1,
  input  in_2,
  input  in_3,
  input  in_4
);

  wire main_1_out_5, main_1_out_6, main_1_out_7, main_1_out_8, main_1_out_9, main_1_out_10, main_1_out_11;

  decoder_main main_1 (
    .w(in_1), .x(in_2), .y(in_3), .z(in_4), .out_5(main_1_out_5), .out_6(main_1_out_6), .out_7(main_1_out_7),
    .out_8(main_1_out_8), .out_9(main_1_out_9), .out_10(main_1_out_10), .out_11(main_1_out_11));
  _7_Segment_Display u_7_segment_display_1 (
    .g(main_1_out_11), .f(main_1_out_5), .a(main_1_out_6), .b(main_1_out_7), .e(main_1_out_10),
    .d(main_1_out_9), .c(main_1_out_8));  // open: dp
endmodule
