// Logisim project sync.mod 10 counter.circ as structural Verilog: 1 circuit, main circuit main
module main (
  output out_1,
  output out_2,
  output out_3,
  output out_4
);

  wire and_1_out, and_2_out, and_3_out, clock_1_out, j_k_ff_1_qn;

  Clock clock_1 (.out(clock_1_out));
  J_K_Flip_Flop j_k_ff_1 (
    .J(and_1_out), .clk(clock_1_out), .K(out_4), .Q(out_1), .Qn(j_k_ff_1_qn));  // open: preset, en, reset
  J_K_Flip_Flop j_k_ff_2 (.J(and_2_out), .clk(clock_1_out), .K(and_2_out), .Q(out_2));  // open: Qn, preset, en, reset
  J_K_Flip_Flop j_k_ff_3 (.J(and_3_out), .clk(clock_1_out), .K(out_4), .Q(out_3));  // open: Qn, preset, en, reset
  J_K_Flip_Flop j_k_ff_4 (.J(1'b1), .clk(clock_1_out), .K(1'b1), .Q(out_4));  // open: Qn, preset, en, reset
  and and_1 (and_1_out, out_2, out_3, out_4);
  and and_2 (and_2_out, out_3, out_4);
  and and_3 (and_3_out, j_k_ff_1_qn, out_4);
endmodule
