// Logisim project universal register.circ as structural Verilog: 1 circuit, main circuit main
module main (
  input  CLR,
  input  I4,
  input  Input_for_LS,
  input  in_4,
  input  I3,
  input  I2,
  input  I1,
  input  So,
  input  S1,
  output A4,
  output A3,
  output A2,
  output A1
);

  wire clock_1_out, main_1_o_p, main_2_o_p, main_3_o_p, main_4_o_p;

  Clock clock_1 (.out(clock_1_out));
  D_Flip_Flop #(.trigger("falling")) d_ff_1 (
    .clk(clock_1_out), .D(main_1_o_p), .Q(A4), .reset(CLR));  // open: Qn, preset, en
  _4X1_MUX_main main_1 (.Io(A4), .I1(I4), .I2(A3), .I3(in_4), .S1(So), .So(S1), .o_p(main_1_o_p));
  D_Flip_Flop #(.trigger("falling")) d_ff_2 (
    .clk(clock_1_out), .D(main_2_o_p), .Q(A3), .reset(CLR));  // open: Qn, preset, en
  _4X1_MUX_main main_2 (.Io(A3), .I1(A4), .I2(A2), .I3(I3), .S1(So), .So(S1), .o_p(main_2_o_p));
  D_Flip_Flop #(.trigger("falling")) d_ff_3 (
    .clk(clock_1_out), .D(main_3_o_p), .Q(A2), .reset(CLR));  // open: Qn, preset, en
  _4X1_MUX_main main_3 (.Io(A2), .I1(A3), .I2(A1), .I3(I2), .S1(So), .So(S1), .o_p(main_3_o_p));
  D_Flip_Flop #(.trigger("falling")) d_ff_4 (
    .clk(clock_1_out), .D(main_4_o_p), .Q(A1), .reset(CLR));  // open: Qn, preset, en
  _4X1_MUX_main main_4 (.Io(A1), .I1(A2), .I2(Input_for_LS), .I3(I1), .S1(So), .So(S1), .o_p(main_4_o_p));

  // Notes on the sheet:
  //   Serial input for right shift
  //   CLK
endmodule
